# Fritzing sketch MaKey-MaKey-Shield (saved by Fritzing 0.9.2b)
perfboards: 1

parts:
  J1 = male pin header, 8 pins [form="♂ (male)"]
  J2 = male pin header, 8 pins [form="♂ (male)"]
  J3 = male pin header, 6 pins [form="♂ (male)"]  # not connected
  J4 = male pin header, 6 pins [form="♂ (male)"]  # not connected
  R1 = Resistor [tolerance=±5% resistance=22k package="1206 [SMD]"]
  R2 = Resistor [tolerance=±5% resistance=22k package="1206 [SMD]"]
  R3 = Resistor [tolerance=±5% resistance=22k package="1206 [SMD]"]
  R4 = Resistor [tolerance=±5% resistance=22k package="1206 [SMD]"]
  R5 = Resistor [tolerance=±5% resistance=22k package="1206 [SMD]"]
  R6 = Resistor [tolerance=±5% resistance=22k package="1206 [SMD]"]
  R7 = Resistor [tolerance=±5% resistance=22k package="1206 [SMD]"]
  R8 = Resistor [tolerance=±5% resistance=22k package="1206 [SMD]"]
  J5 = longpad pin header, 1 pin [form="long pad"]
  J6 = longpad pin header, 1 pin [form="long pad"]
  J7 = longpad pin header, 1 pin [form="long pad"]
  J8 = longpad pin header, 1 pin [form="long pad"]
  J9 = longpad pin header, 1 pin [form="long pad"]
  J10 = longpad pin header, 1 pin [form="long pad"]
  J11 = longpad pin header, 1 pin [form="long pad"]
  J12 = longpad pin header, 1 pin [form="long pad"]
  J13 = longpad pin header, 1 pin [form="long pad"]
  Arduino1 = Arduino Uno (Rev3)

nets:
  N1: J1.pin3, J9.pin1
  N2: J1.pin5, J11.pin1
  N3: J2.pin5, J5.pin1
  N4: J2.pin6, J6.pin1
  N5: J2.pin7, J7.pin1
  N6: R1.Pin_1, R2.Pin_1, R3.Pin_1, R4.Pin_1, R5.Pin_1, R6.Pin_1, R7.Pin_1, R8.Pin_1, Arduino1.5V
  N7: J8.pin1, Arduino1.D8
  N8: J10.pin1, Arduino1.D4
  N9: J12.pin1, Arduino1.D2
  N10: J13.pin1, Arduino1.GND

notes:
  all resistors
  20Mega Ohm
